// Logisim project jk_d.circ as structural Verilog: 1 circuit, main circuit main
module main (
  input  P,
  input  D,
  input  C,
  output out_4,
  output out_5
);

  wire Clk_out, nand_1_out, nand_2_out, nand_3_out, nand_4_out, nand_5_out, nand_6_out, not_1_out, not_2_out;

  Clock Clk (.out(Clk_out));
  not not_1 (not_1_out, D);
  not not_2 (not_2_out, Clk_out);
  nand nand_1 (nand_1_out, D, Clk_out, out_5);
  nand nand_2 (nand_2_out, not_1_out, out_4, Clk_out);
  nand nand_3 (nand_3_out, P, nand_4_out, nand_1_out);
  nand nand_4 (nand_4_out, nand_3_out, C, nand_2_out);
  nand nand_5 (nand_5_out, nand_3_out, not_2_out);
  nand nand_6 (nand_6_out, nand_4_out, not_2_out);
  nand nand_7 (out_4, P, out_5, nand_5_out);
  nand nand_8 (out_5, nand_6_out, nand_6_out, out_4, C);
endmodule
