// Logisim project ULA.circ as structural Verilog: 16 circuits, main circuit ULA
module ULA (
  input  [3:0] \Cálculo ,
  input  C_B_ent,
  input  [7:0] A,
  input  [7:0] B,
  output [7:0] Resultado,
  output OverFlow
);

  wire somador_de_8bits_1_cout, subtrator_8bits_1_bout;
  wire [7:0] and_1_out, deslocador_2bits_di_1_s, deslocador_2bits_esq_1_s, nand_1_out, nor_1_out, not_1_out,
       or_1_out, somador_de_8bits_1_soma, subtrator_8bits_1_s, xor_8bits_1_out_3;

  assign and_1_out = A & B;  // AND_Gate and_1, 8 bits wide
  assign or_1_out = A | B;  // OR_Gate or_1, 8 bits wide
  assign not_1_out = ~A;  // NOT_Gate not_1, 8 bits wide
  assign nand_1_out = ~(A & B);  // NAND_Gate nand_1, 8 bits wide
  assign nor_1_out = ~(A | B);  // NOR_Gate nor_1, 8 bits wide
  xor_8bits xor_8bits_1 (.A(A), .B(B), .out_3(xor_8bits_1_out_3));
  deslocador_2bits_esq deslocador_2bits_esq_1 (.Entra(A), .S(deslocador_2bits_esq_1_s));
  multiplexador_16x1_8bits multiplexador_16x1_8bits_1 (
    .in_1(and_1_out), .in_2(or_1_out), .in_3(not_1_out), .in_4(nor_1_out), .in_5(nand_1_out),
    .in_6(xor_8bits_1_out_3), .in_7(deslocador_2bits_esq_1_s), .in_8(deslocador_2bits_di_1_s),
    .in_9(somador_de_8bits_1_soma), .in_10(subtrator_8bits_1_s), .Select(\Cálculo ), .S(Resultado));
  deslocador_2bits_di deslocador_2bits_di_1 (.Entra(A), .S(deslocador_2bits_di_1_s));
  or or_2 (OverFlow, somador_de_8bits_1_cout, subtrator_8bits_1_bout);
  somador_de_8bits somador_de_8bits_1 (
    .Soma(somador_de_8bits_1_soma), .A(A), .B(B), .Cin(C_B_ent), .Cout(somador_de_8bits_1_cout));
  subtrator_8bits subtrator_8bits_1 (
    .A(A), .B(B), .S(subtrator_8bits_1_s), .Bin(C_B_ent), .Bout(subtrator_8bits_1_bout));
endmodule

module multiplexador_2x1 (
  input  A0,
  input  A1,
  input  Select,
  output S
);

  wire and_1_out, and_2_out, not_1_out;

  not not_1 (not_1_out, Select);
  and and_1 (and_1_out, A0, not_1_out);
  and and_2 (and_2_out, A1, Select);
  or or_1 (S, and_1_out, and_2_out);
endmodule

module multiplexador_2x1_8bits (
  input  [7:0] in_1,
  input  [7:0] in_2,
  input  Select,
  output [7:0] out_4
);

  multiplexador_2x1 multiplexador_2x1_1 (.A0(in_1[0]), .A1(in_2[0]), .Select(Select), .S(out_4[0]));
  multiplexador_2x1 multiplexador_2x1_2 (.A0(in_1[1]), .A1(in_2[1]), .Select(Select), .S(out_4[1]));
  multiplexador_2x1 multiplexador_2x1_3 (.A0(in_1[2]), .A1(in_2[2]), .Select(Select), .S(out_4[2]));
  multiplexador_2x1 multiplexador_2x1_4 (.A0(in_1[3]), .A1(in_2[3]), .Select(Select), .S(out_4[3]));
  multiplexador_2x1 multiplexador_2x1_5 (.A0(in_1[4]), .A1(in_2[4]), .Select(Select), .S(out_4[4]));
  multiplexador_2x1 multiplexador_2x1_6 (.A0(in_1[5]), .A1(in_2[5]), .Select(Select), .S(out_4[5]));
  multiplexador_2x1 multiplexador_2x1_7 (.A0(in_1[6]), .A1(in_2[6]), .Select(Select), .S(out_4[6]));
  multiplexador_2x1 multiplexador_2x1_8 (.A0(in_1[7]), .A1(in_2[7]), .Select(Select), .S(out_4[7]));
endmodule

module multiplexador_4x1_8bits (
  input  [7:0] in_1,
  input  [7:0] in_2,
  input  [7:0] in_3,
  input  [7:0] in_4,
  input  [1:0] Select,
  output [7:0] out_6
);

  wire [7:0] multiplexador_2x1_8bits_1_out_4, multiplexador_2x1_8bits_2_out_4;

  multiplexador_2x1_8bits multiplexador_2x1_8bits_1 (
    .in_1(in_1), .in_2(in_2), .Select(Select[0]), .out_4(multiplexador_2x1_8bits_1_out_4));
  multiplexador_2x1_8bits multiplexador_2x1_8bits_2 (
    .in_1(in_3), .in_2(in_4), .Select(Select[0]), .out_4(multiplexador_2x1_8bits_2_out_4));
  multiplexador_2x1_8bits multiplexador_2x1_8bits_3 (
    .in_1(multiplexador_2x1_8bits_1_out_4), .in_2(multiplexador_2x1_8bits_2_out_4), .Select(Select[1]),
    .out_4(out_6));
endmodule

module multiplexador_8x1_8bits (
  input  [7:0] in_1,
  input  [7:0] in_2,
  input  [7:0] in_3,
  input  [7:0] in_4,
  input  [7:0] in_5,
  input  [7:0] in_6,
  input  [7:0] in_7,
  input  [7:0] in_8,
  input  [2:0] Select,
  output [7:0] S
);

  wire [7:0] multiplexador_4x1_8bits_1_out_6, multiplexador_4x1_8bits_2_out_6;

  multiplexador_4x1_8bits multiplexador_4x1_8bits_1 (
    .in_1(in_1), .in_2(in_2), .in_3(in_3), .in_4(in_4), .Select(Select[1:0]),
    .out_6(multiplexador_4x1_8bits_1_out_6));
  multiplexador_4x1_8bits multiplexador_4x1_8bits_2 (
    .in_1(in_5), .in_2(in_6), .in_3(in_7), .in_4(in_8), .Select(Select[1:0]),
    .out_6(multiplexador_4x1_8bits_2_out_6));
  multiplexador_2x1_8bits multiplexador_2x1_8bits_1 (
    .in_1(multiplexador_4x1_8bits_1_out_6), .in_2(multiplexador_4x1_8bits_2_out_6), .Select(Select[2]),
    .out_4(S));
endmodule

// Multiplexador
module multiplexador_16x1_8bits (
  input  [7:0] in_1,
  input  [7:0] in_2,
  input  [7:0] in_3,
  input  [7:0] in_4,
  input  [7:0] in_5,
  input  [7:0] in_6,
  input  [7:0] in_7,
  input  [7:0] in_8,
  input  [7:0] in_9,
  input  [7:0] in_10,
  input  [3:0] Select,
  output [7:0] S
);

  wire [7:0] multiplexador_8x1_8bits_1_s, multiplexador_8x1_8bits_2_s;

  multiplexador_8x1_8bits multiplexador_8x1_8bits_1 (
    .in_1(in_1), .in_2(in_2), .in_3(in_3), .in_4(in_4), .in_5(in_5), .in_6(in_6), .in_7(in_7), .in_8(in_8),
    .Select(Select[2:0]), .S(multiplexador_8x1_8bits_1_s));
  multiplexador_8x1_8bits multiplexador_8x1_8bits_2 (
    .in_1(in_9), .in_2(in_10), .Select(Select[2:0]), .S(multiplexador_8x1_8bits_2_s));  // open: in_3, in_4, in_5, in_6, in_7, in_8
  multiplexador_2x1_8bits multiplexador_2x1_8bits_1 (
    .in_1(multiplexador_8x1_8bits_1_s), .in_2(multiplexador_8x1_8bits_2_s), .Select(Select[3]), .out_4(S));
endmodule

// XOR
module \xor  (
  input  A,
  input  B,
  output S
);

  wire and_1_out, and_2_out, not_1_out, not_2_out;

  not not_1 (not_1_out, B);
  and and_1 (and_1_out, not_1_out, A);
  or or_1 (S, and_1_out, and_2_out);
  not not_2 (not_2_out, A);
  and and_2 (and_2_out, not_2_out, B);
endmodule

// XOR
module xor_8bits (
  input  [7:0] A,
  input  [7:0] B,
  output [7:0] out_3
);

  \xor  xor_1 (.A(A[0]), .B(B[0]), .S(out_3[0]));
  \xor  xor_2 (.A(A[1]), .B(B[1]), .S(out_3[1]));
  \xor  xor_3 (.A(A[2]), .B(B[2]), .S(out_3[2]));
  \xor  xor_4 (.A(A[3]), .B(B[3]), .S(out_3[3]));
  \xor  xor_5 (.A(A[4]), .B(B[4]), .S(out_3[4]));
  \xor  xor_6 (.A(A[6]), .B(B[6]), .S(out_3[6]));
  \xor  xor_7 (.A(A[5]), .B(B[5]), .S(out_3[5]));
  \xor  xor_8 (.A(A[7]), .B(B[7]), .S(out_3[7]));
endmodule

// Sum
module somador (
  input  A,
  input  B,
  input  Cin,
  output Soma,
  output Cout
);

  wire and_1_out, and_2_out, xor_1_s;

  \xor  xor_1 (.A(A), .B(B), .S(xor_1_s));
  and and_1 (and_1_out, B, A);
  or or_1 (Cout, and_1_out, and_2_out);
  \xor  xor_2 (.A(xor_1_s), .B(Cin), .S(Soma));
  and and_2 (and_2_out, Cin, xor_1_s);
endmodule

// SOM
module somador_de_8bits (
  input  [7:0] A,
  input  Cin,
  input  [7:0] B,
  output [7:0] Soma,
  output Cout
);

  wire somador_1_cout, somador_2_cout, somador_3_cout, somador_4_cout, somador_5_cout, somador_6_cout,
       somador_7_cout;

  somador somador_1 (.A(A[0]), .B(B[0]), .Cin(Cin), .Cout(somador_1_cout), .Soma(Soma[0]));
  somador somador_2 (.A(A[4]), .B(B[4]), .Cin(somador_7_cout), .Cout(somador_2_cout), .Soma(Soma[4]));
  somador somador_3 (.A(A[1]), .B(B[1]), .Cin(somador_1_cout), .Cout(somador_3_cout), .Soma(Soma[1]));
  somador somador_4 (.A(A[5]), .B(B[5]), .Cin(somador_2_cout), .Cout(somador_4_cout), .Soma(Soma[5]));
  somador somador_5 (.A(A[2]), .B(B[2]), .Cin(somador_3_cout), .Cout(somador_5_cout), .Soma(Soma[2]));
  somador somador_6 (.A(A[6]), .B(B[6]), .Cin(somador_4_cout), .Cout(somador_6_cout), .Soma(Soma[6]));
  somador somador_7 (.A(A[3]), .B(B[3]), .Cin(somador_5_cout), .Cout(somador_7_cout), .Soma(Soma[3]));
  somador somador_8 (.A(A[7]), .B(B[7]), .Cin(somador_6_cout), .Cout(Cout), .Soma(Soma[7]));
endmodule

// Subt
module subtrator (
  input  A,
  input  B,
  input  Bin,
  output S,
  output Bout
);

  wire and_1_out, and_2_out, not_1_out, not_2_out, xor_1_s;

  not not_1 (not_1_out, A);
  and and_1 (and_1_out, B, not_1_out);
  \xor  xor_1 (.A(A), .B(B), .S(xor_1_s));
  \xor  xor_2 (.A(xor_1_s), .B(Bin), .S(S));
  or or_1 (Bout, and_1_out, and_2_out);
  not not_2 (not_2_out, xor_1_s);
  and and_2 (and_2_out, Bin, not_2_out);
endmodule

// SUB
module subtrator_8bits (
  input  [7:0] A,
  input  Bin,
  input  [7:0] B,
  output [7:0] S,
  output Bout
);

  wire subtrator_1_bout, subtrator_2_bout, subtrator_3_bout, subtrator_4_bout, subtrator_5_bout,
       subtrator_6_bout, subtrator_7_bout;

  subtrator subtrator_1 (.A(A[0]), .B(B[0]), .Bin(Bin), .S(S[0]), .Bout(subtrator_1_bout));
  subtrator subtrator_2 (.A(A[4]), .B(B[4]), .Bin(subtrator_7_bout), .S(S[4]), .Bout(subtrator_2_bout));
  subtrator subtrator_3 (.A(A[1]), .B(B[1]), .Bin(subtrator_1_bout), .S(S[1]), .Bout(subtrator_3_bout));
  subtrator subtrator_4 (.A(A[5]), .B(B[5]), .Bin(subtrator_2_bout), .S(S[5]), .Bout(subtrator_4_bout));
  subtrator subtrator_5 (.A(A[2]), .B(B[2]), .Bin(subtrator_3_bout), .S(S[2]), .Bout(subtrator_5_bout));
  subtrator subtrator_6 (.A(A[6]), .B(B[6]), .Bin(subtrator_4_bout), .S(S[6]), .Bout(subtrator_6_bout));
  subtrator subtrator_7 (.A(A[3]), .B(B[3]), .Bin(subtrator_5_bout), .S(S[3]), .Bout(subtrator_7_bout));
  subtrator subtrator_8 (.A(A[7]), .B(B[7]), .Bin(subtrator_6_bout), .S(S[7]), .Bout(Bout));
endmodule

module deslocador_1bit_di (
  input  [7:0] in_1,
  output [7:0] out_2
);

  wire and_1_out, and_3_out, and_4_out, and_5_out, and_6_out, and_7_out, and_8_out, and_9_out, and_10_out,
       and_11_out, and_12_out, and_14_out, not_1_out;

  not not_1 (not_1_out, 1'b0);
  and and_1 (and_1_out, in_1[7], not_1_out);
  and and_2 (out_2[7], 1'b0, in_1[6]);
  and and_3 (and_3_out, in_1[6], not_1_out);
  and and_4 (and_4_out, 1'b0, in_1[5]);
  and and_5 (and_5_out, in_1[5], not_1_out);
  and and_6 (and_6_out, 1'b0, in_1[4]);
  and and_7 (and_7_out, in_1[4], not_1_out);
  and and_8 (and_8_out, 1'b0, in_1[3]);
  and and_9 (and_9_out, in_1[3], not_1_out);
  and and_10 (and_10_out, 1'b0, in_1[2]);
  and and_11 (and_11_out, in_1[2], not_1_out);
  and and_12 (and_12_out, 1'b0, in_1[1]);
  and and_13 (out_2[0], in_1[1], not_1_out);
  and and_14 (and_14_out, 1'b0, in_1[0]);
  or or_1 (out_2[6], and_1_out, and_4_out);
  or or_2 (out_2[5], and_3_out, and_6_out);
  or or_3 (out_2[4], and_5_out, and_8_out);
  or or_4 (out_2[3], and_7_out, and_10_out);
  or or_5 (out_2[2], and_9_out, and_12_out);
  or or_6 (out_2[1], and_11_out, and_14_out);
endmodule

module deslocador_2bits_di (
  input  [7:0] Entra,
  output [7:0] S
);

  wire [7:0] deslocador_1bit_di_1_out_2;

  deslocador_1bit_di deslocador_1bit_di_1 (.in_1(Entra), .out_2(deslocador_1bit_di_1_out_2));
  deslocador_1bit_di deslocador_1bit_di_2 (.in_1(deslocador_1bit_di_1_out_2), .out_2(S));
endmodule

module deslocador_1bit_esq (
  input  [7:0] in_1,
  output [7:0] out_2
);

  wire and_1_out, and_3_out, and_4_out, and_5_out, and_6_out, and_7_out, and_8_out, and_9_out, and_10_out,
       and_11_out, and_12_out, and_14_out, not_1_out;

  not not_1 (not_1_out, 1'b1);
  and and_1 (and_1_out, in_1[7], not_1_out);
  and and_2 (out_2[7], 1'b1, in_1[6]);
  and and_3 (and_3_out, in_1[6], not_1_out);
  and and_4 (and_4_out, 1'b1, in_1[5]);
  and and_5 (and_5_out, in_1[5], not_1_out);
  and and_6 (and_6_out, 1'b1, in_1[4]);
  and and_7 (and_7_out, in_1[4], not_1_out);
  and and_8 (and_8_out, 1'b1, in_1[3]);
  and and_9 (and_9_out, in_1[3], not_1_out);
  and and_10 (and_10_out, 1'b1, in_1[2]);
  and and_11 (and_11_out, in_1[2], not_1_out);
  and and_12 (and_12_out, 1'b1, in_1[1]);
  and and_13 (out_2[0], in_1[1], not_1_out);
  and and_14 (and_14_out, 1'b1, in_1[0]);
  or or_1 (out_2[6], and_1_out, and_4_out);
  or or_2 (out_2[5], and_3_out, and_6_out);
  or or_3 (out_2[4], and_5_out, and_8_out);
  or or_4 (out_2[3], and_7_out, and_10_out);
  or or_5 (out_2[2], and_9_out, and_12_out);
  or or_6 (out_2[1], and_11_out, and_14_out);
endmodule

module deslocador_2bits_esq (
  input  [7:0] Entra,
  output [7:0] S
);

  wire [7:0] deslocador_1bit_esq_1_out_2;

  deslocador_1bit_esq deslocador_1bit_esq_1 (.in_1(Entra), .out_2(deslocador_1bit_esq_1_out_2));
  deslocador_1bit_esq deslocador_1bit_esq_2 (.in_1(deslocador_1bit_esq_1_out_2), .out_2(S));
endmodule
