// Logisim project contador_sincrono.circ as structural Verilog: 2 circuits, main circuit main
module main (
  input  in_1,
  input  in_2,
  input  in_3,
  input  in_4,
  output out_5,
  output out_6,
  output out_7,
  output out_8
);

  wire and_1_out, and_2_out;

  jk jk_1 ();  // open: j, clk, k, p, c, Q, out_7
  jk jk_2 (.j(and_1_out), .clk(in_2), .k(and_1_out), .p(in_1), .c(in_3), .Q(out_7));  // open: out_7
  and and_1 (and_1_out, out_5, and_2_out);
  jk jk_3 (.j(and_2_out), .clk(in_2), .k(and_2_out), .p(in_1), .c(in_3), .Q(out_5));  // open: out_7
  and and_2 (and_2_out, out_6, out_8);
  jk jk_4 (.j(out_8), .clk(in_2), .k(out_8), .p(in_1), .c(in_3), .Q(out_6));  // open: out_7
  jk jk_5 (.j(in_4), .clk(in_2), .k(in_4), .p(in_1), .c(in_3), .Q(out_8));  // open: out_7
endmodule

module jk (
  input  p,
  input  j,
  input  clk,
  input  k,
  input  c,
  output Q,
  output out_7
);

  wire nand_1_out, nand_2_out, nand_3_out, nand_4_out, nand_5_out, nand_6_out, not_1_out;

  nand nand_1 (nand_1_out, j, clk, out_7);
  nand nand_2 (nand_2_out, Q, clk, k);
  not not_1 (not_1_out, clk);
  nand nand_3 (nand_3_out, p, nand_1_out, nand_4_out);
  nand nand_4 (nand_4_out, nand_3_out, nand_2_out, c);
  nand nand_5 (nand_5_out, not_1_out, nand_3_out);
  nand nand_6 (nand_6_out, nand_4_out, not_1_out);
  nand nand_7 (Q, p, nand_5_out, out_7);
  nand nand_8 (out_7, nand_6_out, Q, c);
endmodule
