// Logisim project otimização_lógica_karnaugh.circ as structural Verilog: 1 circuit, main circuit main
module main (
  input  A,
  input  C,
  input  B,
  input  B_2,
  input  C_2,
  input  A_2,
  output Z,
  output Z_2
);

  wire and_1_out, and_3_out, nand_1_out, not_1_out, not_2_out, not_3_out, not_4_out, or_1_out;

  not not_1 (not_1_out, A);
  not not_2 (not_2_out, C);
  not not_3 (not_3_out, B_2);
  nand nand_1 (nand_1_out, not_1_out, not_2_out);
  and and_1 (and_1_out, A, C, B);
  or or_1 (or_1_out, not_3_out, C_2);
  not not_4 (not_4_out, B);
  and and_2 (Z_2, or_1_out, A_2);
  and and_3 (and_3_out, nand_1_out, A, not_4_out);
  or or_2 (Z, and_3_out, and_1_out);

  // Notes on the sheet:
  //   Circuito original:
  //   Circuito simplificado:
  //   ~(~A ~C) A ~B + A C B
  //   (~B + C) A
endmodule
