// Logisim project decodificador_7_segmentos.circ as structural Verilog: 8 circuits, main circuit decodificador_7segmentos
module etapa1 (
  input  [3:0] in_1,
  output out_2
);

  wire and_1_out, and_2_out, and_3_out, and_4_out, and_5_out, and_6_out, not_1_out, not_2_out, not_3_out,
       not_4_out, not_5_out, not_6_out, not_7_out;

  not not_1 (not_1_out, in_1[1]);
  not not_2 (not_2_out, in_1[0]);
  not not_3 (not_3_out, in_1[2]);
  and and_1 (and_1_out, not_1_out, not_3_out, in_1[3]);
  and and_2 (and_2_out, not_2_out, in_1[3]);
  and and_3 (and_3_out, in_1[1], in_1[1]);
  not not_4 (not_4_out, in_1[3]);
  and and_4 (and_4_out, in_1[0], in_1[2], not_4_out);
  or or_1 (out_2, and_1_out, and_2_out, and_3_out, and_4_out, and_5_out, and_6_out);
  not not_5 (not_5_out, in_1[3]);
  and and_5 (and_5_out, in_1[1], not_5_out);
  not not_6 (not_6_out, in_1[0]);
  not not_7 (not_7_out, in_1[2]);
  and and_6 (and_6_out, not_6_out, not_7_out);
endmodule

module etapa2 (
  input  [3:0] in_1,
  output out_2
);

  wire and_1_out, and_2_out, and_3_out, and_4_out, and_5_out, not_1_out, not_2_out, not_3_out, not_4_out,
       not_5_out, not_6_out, not_7_out, not_8_out, not_9_out;

  not not_1 (not_1_out, in_1[3]);
  not not_2 (not_2_out, in_1[2]);
  and and_1 (and_1_out, not_2_out, not_1_out);
  and and_2 (and_2_out, in_1[0], in_1[1], not_6_out);
  not not_3 (not_3_out, in_1[1]);
  not not_4 (not_4_out, in_1[0]);
  not not_5 (not_5_out, in_1[2]);
  not not_6 (not_6_out, in_1[3]);
  and and_3 (and_3_out, not_4_out, not_3_out, not_5_out);
  or or_1 (out_2, and_1_out, and_2_out, and_3_out, and_4_out, and_5_out);
  not not_7 (not_7_out, in_1[0]);
  not not_8 (not_8_out, in_1[1]);
  not not_9 (not_9_out, in_1[2]);
  and and_4 (and_4_out, not_7_out, not_9_out);
  and and_5 (and_5_out, in_1[0], not_8_out, in_1[3]);
endmodule

module etapa3 (
  input  [3:0] in_1,
  output out_2
);

  wire and_1_out, and_2_out, and_3_out, and_4_out, and_5_out, not_1_out, not_2_out, not_3_out, not_4_out,
       not_5_out, not_6_out;

  not not_1 (not_1_out, in_1[3]);
  and and_1 (and_1_out, in_1[0], not_1_out);
  not not_2 (not_2_out, in_1[3]);
  not not_3 (not_3_out, in_1[1]);
  and and_2 (and_2_out, not_3_out, not_2_out);
  not not_4 (not_4_out, in_1[2]);
  and and_3 (and_3_out, in_1[2], not_5_out);
  and and_4 (and_4_out, not_4_out, in_1[3]);
  or or_1 (out_2, and_1_out, and_2_out, and_4_out, and_3_out, and_5_out);
  not not_5 (not_5_out, in_1[3]);
  not not_6 (not_6_out, in_1[1]);
  and and_5 (and_5_out, in_1[0], not_6_out);
endmodule

module etapa4 (
  input  [3:0] in_1,
  output out_2
);

  wire and_1_out, and_2_out, and_3_out, and_4_out, and_5_out, not_1_out, not_2_out, not_3_out, not_4_out,
       not_5_out, not_6_out, not_7_out;

  not not_1 (not_1_out, in_1[2]);
  not not_2 (not_2_out, in_1[1]);
  not not_3 (not_3_out, in_1[3]);
  not not_4 (not_4_out, in_1[0]);
  and and_1 (and_1_out, not_2_out, in_1[3]);
  and and_2 (and_2_out, not_4_out, not_1_out, not_3_out);
  not not_5 (not_5_out, in_1[0]);
  and and_3 (and_3_out, not_5_out, in_1[1], in_1[2]);
  or or_1 (out_2, and_2_out, and_1_out, and_3_out, and_4_out, and_5_out);
  // NOT_Gate not_6 has open pins: in=open, out=not_6_out
  not not_7 (not_7_out, in_1[1]);
  and and_4 (and_4_out, in_1[0], in_1[1], not_6_out);
  and and_5 (and_5_out, in_1[0], not_7_out, in_1[2]);
endmodule

module etapa5 (
  input  [3:0] in_1,
  output out_2
);

  wire and_1_out, and_2_out, and_3_out, and_4_out, not_1_out, not_2_out, not_3_out;

  and and_1 (and_1_out, in_1[2], in_1[3]);
  not not_1 (not_1_out, in_1[0]);
  and and_2 (and_2_out, not_1_out, in_1[1]);
  and and_3 (and_3_out, in_1[1], in_1[3]);
  or or_1 (out_2, and_1_out, and_3_out, and_2_out, and_4_out);
  not not_2 (not_2_out, in_1[2]);
  not not_3 (not_3_out, in_1[0]);
  and and_4 (and_4_out, not_3_out, not_2_out);
endmodule

module etapa6 (
  input  [3:0] in_1,
  output out_2
);

  wire and_1_out, and_2_out, and_3_out, and_4_out, and_5_out, not_1_out, not_2_out, not_3_out, not_4_out,
       not_5_out, not_6_out;

  and and_1 (and_1_out, in_1[1], in_1[3]);
  not not_1 (not_1_out, in_1[3]);
  and and_2 (and_2_out, not_1_out, in_1[3]);
  not not_2 (not_2_out, in_1[3]);
  not not_3 (not_3_out, in_1[1]);
  and and_3 (and_3_out, not_3_out, in_1[3], not_2_out);
  or or_1 (out_2, and_1_out, and_2_out, and_3_out, and_4_out, and_5_out);
  not not_4 (not_4_out, in_1[0]);
  and and_4 (and_4_out, not_4_out, in_1[3]);
  not not_5 (not_5_out, in_1[1]);
  not not_6 (not_6_out, in_1[0]);
  and and_5 (and_5_out, not_6_out, not_5_out);

  assign in_1[2] = in_1[3];
endmodule

module etapa7 (
  input  [3:0] in_1,
  output out_2
);

  wire and_1_out, and_2_out, and_3_out, and_4_out, and_5_out, not_1_out, not_2_out, not_3_out, not_4_out,
       not_5_out;

  not not_1 (not_1_out, in_1[3]);
  not not_2 (not_2_out, in_1[1]);
  and and_1 (and_1_out, not_2_out, in_1[2], not_1_out);
  not not_3 (not_3_out, in_1[0]);
  and and_2 (and_2_out, not_3_out, in_1[1]);
  not not_4 (not_4_out, in_1[2]);
  and and_3 (and_3_out, not_4_out, in_1[3]);
  and and_4 (and_4_out, in_1[0], in_1[3]);
  or or_1 (out_2, and_1_out, and_2_out, and_4_out, and_3_out, and_5_out);
  not not_5 (not_5_out, in_1[3]);
  and and_5 (and_5_out, in_1[1], not_5_out);
endmodule

module decodificador_7segmentos (
  input  [3:0] in_1
);

  wire etapa1_1_out_2, etapa2_1_out_2, etapa3_1_out_2, etapa4_1_out_2, etapa5_1_out_2, etapa6_1_out_2,
       etapa7_1_out_2;

  etapa1 etapa1_1 (.in_1(in_1), .out_2(etapa1_1_out_2));
  etapa2 etapa2_1 (.in_1(in_1), .out_2(etapa2_1_out_2));
  etapa3 etapa3_1 (.in_1(in_1), .out_2(etapa3_1_out_2));
  etapa4 etapa4_1 (.in_1(in_1), .out_2(etapa4_1_out_2));
  etapa5 etapa5_1 (.in_1(in_1), .out_2(etapa5_1_out_2));
  etapa6 etapa6_1 (.in_1(in_1), .out_2(etapa6_1_out_2));
  etapa7 etapa7_1 (.in_1(in_1), .out_2(etapa7_1_out_2));
  _7_Segment_Display u_7_segment_display_1 (
    .g(etapa7_1_out_2), .f(etapa6_1_out_2), .a(etapa1_1_out_2), .b(etapa2_1_out_2), .e(etapa5_1_out_2),
    .d(etapa4_1_out_2), .c(etapa3_1_out_2));  // open: dp
endmodule
