// Logisim project multiplexador.circ as structural Verilog: 1 circuit, main circuit multiplexador
module multiplexador (
  input  A,
  input  B,
  input  C,
  input  D,
  input  Seletor_1,
  input  Seletor_2,
  output \Saída 
);

  wire and_1_out, and_2_out, and_3_out, and_4_out, not_1_out, not_2_out;

  not not_1 (not_1_out, Seletor_1);
  not not_2 (not_2_out, Seletor_2);
  and and_1 (and_1_out, A, Seletor_1, Seletor_2);
  and and_2 (and_2_out, B, not_1_out, Seletor_2);
  and and_3 (and_3_out, C, not_2_out, Seletor_1);
  and and_4 (and_4_out, D, not_1_out, not_2_out);
  or or_1 (\Saída , and_1_out, and_2_out, and_3_out, and_4_out);

  // Notes on the sheet:
  //   SELETORES 1 E 2             SAÍDA
  //   CASO 00
  //   CASO 01
  //   CASO 10
  //   CASO 11
  //   D
  //   B
  //   C
  //   A
endmodule
