// Logisim project XOR.circ as structural Verilog: 1 circuit, main circuit XOR
module XOR (
  input  A0,
  input  A1,
  output \Saída 
);

  wire and_1_out, and_2_out, not_1_out, not_2_out;

  not not_1 (not_1_out, A0);
  not not_2 (not_2_out, A1);
  and and_1 (and_1_out, not_1_out, A1);
  and and_2 (and_2_out, A0, not_2_out);
  or or_1 (\Saída , and_1_out, and_2_out);
endmodule
