// Logisim project somador8bits_com 4.circ as structural Verilog: 3 circuits, main circuit Somador 8 bits_soma com 4
module main (
  input  A,
  input  B,
  input  Te,
  output S,
  output Ts
);

  wire and_1_out, and_2_out, and_3_out, xor_1_out;

  xor xor_1 (xor_1_out, A, B);
  and and_1 (and_1_out, B, Te);
  and and_2 (and_2_out, Te, A);
  and and_3 (and_3_out, B, A);
  xor xor_2 (S, xor_1_out, Te);
  or or_1 (Ts, and_1_out, and_2_out, and_3_out);
endmodule

module Somador_de_8_bits (
  input  in_1,
  input  in_2,
  input  in_3,
  input  in_4,
  input  in_5,
  input  in_6,
  input  in_7,
  input  in_8,
  input  in_9,
  input  in_10,
  input  in_11,
  input  in_12,
  input  in_13,
  input  in_14,
  input  in_15,
  input  in_16,
  input  in_17,
  output out_18,
  output out_19,
  output out_20,
  output out_21,
  output out_22,
  output out_23,
  output out_24,
  output out_25,
  output out_26
);

  wire main_1_ts, main_2_ts, main_3_ts, main_4_ts, main_5_ts, main_6_ts, main_7_ts;

  main main_1 (.A(in_1), .B(in_2), .Te(in_3), .S(out_18), .Ts(main_1_ts));
  main main_2 (.A(in_4), .B(in_5), .Te(main_1_ts), .S(out_19), .Ts(main_2_ts));
  main main_3 (.A(in_6), .B(in_7), .Te(main_2_ts), .S(out_20), .Ts(main_3_ts));
  main main_4 (.A(in_8), .B(in_9), .Te(main_3_ts), .S(out_21), .Ts(main_4_ts));
  main main_5 (.A(in_10), .B(in_11), .Te(main_4_ts), .S(out_22), .Ts(main_5_ts));
  main main_6 (.A(in_12), .B(in_13), .Te(main_5_ts), .S(out_23), .Ts(main_6_ts));
  main main_7 (.A(in_14), .B(in_15), .Te(main_6_ts), .S(out_24), .Ts(main_7_ts));
  main main_8 (.A(in_16), .B(in_17), .Te(main_7_ts), .S(out_25), .Ts(out_26));
endmodule

module Somador_8_bits_soma_com_4 (
  input  [7:0] in_1,
  input  in_2,
  output [7:0] \Saída ,
  output Estouro
);

  Somador_de_8_bits somador_de_8_bits_1 (
    .in_1(in_1[0]), .in_2(1'b0), .in_3(in_2), .in_4(in_1[1]), .in_5(1'b0), .in_6(in_1[2]), .in_7(1'b1),
    .in_8(in_1[3]), .in_9(1'b0), .in_10(in_1[4]), .in_11(1'b0), .in_12(in_1[5]), .in_13(1'b0),
    .in_14(in_1[6]), .in_15(1'b0), .in_16(in_1[7]), .in_17(1'b0), .out_18(\Saída [0]), .out_19(\Saída [1]),
    .out_20(\Saída [2]), .out_21(\Saída [3]), .out_22(\Saída [4]), .out_23(\Saída [5]), .out_24(\Saída [6]),
    .out_25(\Saída [7]), .out_26(Estouro));
endmodule
