// Logisim project memória_ram.circ as structural Verilog: 8 circuits, main circuit main
module main (
  input  PRESET,
  input  D,
  input  CLK,
  input  CLEAR,
  output Q,
  output nQ
);

  wire nand_1_out, nand_2_out, nand_3_out, nand_4_out, nand_5_out, nand_6_out, not_1_out, not_2_out,
       not_3_out, not_4_out;

  not not_1 (not_1_out, D);
  nand nand_1 (nand_1_out, nQ, D, CLK);
  not not_2 (not_2_out, CLK);
  nand nand_2 (nand_2_out, CLK, not_1_out, Q);
  not not_3 (not_3_out, PRESET);
  not not_4 (not_4_out, CLEAR);
  nand nand_3 (nand_3_out, not_3_out, nand_1_out, nand_4_out);
  nand nand_4 (nand_4_out, nand_3_out, nand_2_out, not_4_out);
  nand nand_5 (nand_5_out, not_4_out, nand_3_out, not_2_out);
  nand nand_6 (nand_6_out, not_2_out, nand_4_out, not_3_out);
  nand nand_7 (Q, not_3_out, nand_5_out, nQ);
  nand nand_8 (nQ, Q, nand_6_out, not_4_out);
endmodule

module registrador_8bits (
  input  [7:0] in_1,
  input  PRESET,
  input  CLEAR,
  input  CLK,
  output [7:0] out_5
);

  main main_1 (.PRESET(PRESET), .D(in_1[0]), .CLK(CLK), .CLEAR(CLEAR), .Q(out_5[0]));  // open: nQ
  main main_2 (.PRESET(PRESET), .D(in_1[1]), .CLK(CLK), .CLEAR(CLEAR), .Q(out_5[1]));  // open: nQ
  main main_3 (.PRESET(PRESET), .D(in_1[2]), .CLK(CLK), .CLEAR(CLEAR), .Q(out_5[2]));  // open: nQ
  main main_4 (.PRESET(PRESET), .D(in_1[3]), .CLK(CLK), .CLEAR(CLEAR), .Q(out_5[3]));  // open: nQ
  main main_5 (.PRESET(PRESET), .D(in_1[4]), .CLK(CLK), .CLEAR(CLEAR), .Q(out_5[4]));  // open: nQ
  main main_6 (.PRESET(PRESET), .D(in_1[5]), .CLK(CLK), .CLEAR(CLEAR), .Q(out_5[5]));  // open: nQ
  main main_7 (.PRESET(PRESET), .D(in_1[6]), .CLK(CLK), .CLEAR(CLEAR), .Q(out_5[6]));  // open: nQ
  main main_8 (.PRESET(PRESET), .D(in_1[7]), .CLK(CLK), .CLEAR(CLEAR), .Q(out_5[7]));  // open: nQ
endmodule

module demux_1x8 (
  input  [2:0] in_1,
  input  Data_input,
  output out_3,
  output out_4,
  output out_5,
  output out_6,
  output out_7,
  output out_8,
  output out_9,
  output out_10
);

  wire not_1_out, not_2_out, not_3_out;

  not not_1 (not_1_out, in_1[2]);
  not not_2 (not_2_out, in_1[1]);
  not not_3 (not_3_out, in_1[0]);
  and _0 (out_3, not_1_out, not_2_out, not_3_out, Data_input);
  and _1 (out_4, not_1_out, not_2_out, in_1[0], Data_input);
  and _2 (out_5, not_1_out, in_1[1], not_3_out, Data_input);
  and _3 (out_6, not_1_out, in_1[1], in_1[0], Data_input);
  and _4 (out_7, in_1[2], not_2_out, not_3_out, Data_input);
  and _5 (out_8, in_1[2], not_2_out, in_1[0], Data_input);
  and _6 (out_9, in_1[1], in_1[2], not_3_out, Data_input);
  and _7 (out_10, in_1[1], in_1[2], in_1[0], Data_input);
endmodule

module multiplexador_2x1 (
  input  A0,
  input  A1,
  input  Select,
  output S
);

  wire and_1_out, and_2_out, not_1_out;

  not not_1 (not_1_out, Select);
  and and_1 (and_1_out, A0, not_1_out);
  and and_2 (and_2_out, A1, Select);
  or or_1 (S, and_1_out, and_2_out);
endmodule

module multiplexador_2x1_8bits (
  input  [7:0] in_1,
  input  [7:0] in_2,
  input  Select,
  output [7:0] out_4
);

  multiplexador_2x1 multiplexador_2x1_1 (.A0(in_1[0]), .A1(in_2[0]), .Select(Select), .S(out_4[0]));
  multiplexador_2x1 multiplexador_2x1_2 (.A0(in_1[1]), .A1(in_2[1]), .Select(Select), .S(out_4[1]));
  multiplexador_2x1 multiplexador_2x1_3 (.A0(in_1[2]), .A1(in_2[2]), .Select(Select), .S(out_4[2]));
  multiplexador_2x1 multiplexador_2x1_4 (.A0(in_1[3]), .A1(in_2[3]), .Select(Select), .S(out_4[3]));
  multiplexador_2x1 multiplexador_2x1_5 (.A0(in_1[4]), .A1(in_2[4]), .Select(Select), .S(out_4[4]));
  multiplexador_2x1 multiplexador_2x1_6 (.A0(in_1[5]), .A1(in_2[5]), .Select(Select), .S(out_4[5]));
  multiplexador_2x1 multiplexador_2x1_7 (.A0(in_1[6]), .A1(in_2[6]), .Select(Select), .S(out_4[6]));
  multiplexador_2x1 multiplexador_2x1_8 (.A0(in_1[7]), .A1(in_2[7]), .Select(Select), .S(out_4[7]));
endmodule

module multiplexador_4x1_8bits (
  input  [7:0] in_1,
  input  [7:0] in_2,
  input  [7:0] in_3,
  input  [7:0] in_4,
  input  [1:0] Select,
  output [7:0] out_6
);

  wire [7:0] multiplexador_2x1_8bits_1_out_4, multiplexador_2x1_8bits_2_out_4;

  multiplexador_2x1_8bits multiplexador_2x1_8bits_1 (
    .in_1(in_1), .in_2(in_2), .Select(Select[0]), .out_4(multiplexador_2x1_8bits_1_out_4));
  multiplexador_2x1_8bits multiplexador_2x1_8bits_2 (
    .in_1(in_3), .in_2(in_4), .Select(Select[0]), .out_4(multiplexador_2x1_8bits_2_out_4));
  multiplexador_2x1_8bits multiplexador_2x1_8bits_3 (
    .in_1(multiplexador_2x1_8bits_1_out_4), .in_2(multiplexador_2x1_8bits_2_out_4), .Select(Select[1]),
    .out_4(out_6));
endmodule

module multiplexador_8x1_8bits (
  input  [7:0] in_1,
  input  [7:0] in_2,
  input  [7:0] in_3,
  input  [7:0] in_4,
  input  [7:0] in_5,
  input  [7:0] in_6,
  input  [7:0] in_7,
  input  [7:0] in_8,
  input  [2:0] in_9,
  output [7:0] out_10
);

  wire [7:0] multiplexador_4x1_8bits_1_out_6, multiplexador_4x1_8bits_2_out_6;

  multiplexador_4x1_8bits multiplexador_4x1_8bits_1 (
    .in_1(in_1), .in_2(in_2), .in_3(in_3), .in_4(in_4), .Select(in_9[1:0]),
    .out_6(multiplexador_4x1_8bits_1_out_6));
  multiplexador_4x1_8bits multiplexador_4x1_8bits_2 (
    .in_1(in_5), .in_2(in_6), .in_3(in_7), .in_4(in_8), .Select(in_9[1:0]),
    .out_6(multiplexador_4x1_8bits_2_out_6));
  multiplexador_2x1_8bits multiplexador_2x1_8bits_1 (
    .in_1(multiplexador_4x1_8bits_1_out_6), .in_2(multiplexador_4x1_8bits_2_out_6), .Select(in_9[2]),
    .out_4(out_10));
endmodule

module \memória_ram  (
  input  [2:0] in_1,
  input  [7:0] INPUT,
  input  PRESET,
  input  CLEAR,
  output [7:0] out_5
);

  wire clock_1_out, demux_1x8_1_out_3, demux_1x8_1_out_4, demux_1x8_1_out_5, demux_1x8_1_out_6,
       demux_1x8_1_out_7, demux_1x8_1_out_8, demux_1x8_1_out_9, demux_1x8_1_out_10;
  wire [7:0] registrador_8bits_1_out_5, registrador_8bits_2_out_5, registrador_8bits_3_out_5,
       registrador_8bits_4_out_5, registrador_8bits_5_out_5, registrador_8bits_6_out_5,
       registrador_8bits_7_out_5, registrador_8bits_8_out_5;

  Clock clock_1 (.out(clock_1_out));
  demux_1x8 demux_1x8_1 (
    .in_1(in_1), .Data_input(clock_1_out), .out_3(demux_1x8_1_out_3), .out_4(demux_1x8_1_out_4),
    .out_5(demux_1x8_1_out_5), .out_6(demux_1x8_1_out_6), .out_7(demux_1x8_1_out_7),
    .out_8(demux_1x8_1_out_8), .out_9(demux_1x8_1_out_9), .out_10(demux_1x8_1_out_10));
  registrador_8bits registrador_8bits_1 (
    .in_1(INPUT), .PRESET(PRESET), .CLEAR(CLEAR), .CLK(demux_1x8_1_out_3), .out_5(registrador_8bits_1_out_5));
  registrador_8bits registrador_8bits_2 (
    .in_1(INPUT), .PRESET(PRESET), .CLEAR(CLEAR), .CLK(demux_1x8_1_out_4), .out_5(registrador_8bits_2_out_5));
  registrador_8bits registrador_8bits_3 (
    .in_1(INPUT), .PRESET(PRESET), .CLEAR(CLEAR), .CLK(demux_1x8_1_out_5), .out_5(registrador_8bits_3_out_5));
  registrador_8bits registrador_8bits_4 (
    .in_1(INPUT), .PRESET(PRESET), .CLEAR(CLEAR), .CLK(demux_1x8_1_out_6), .out_5(registrador_8bits_4_out_5));
  registrador_8bits registrador_8bits_5 (
    .in_1(INPUT), .PRESET(PRESET), .CLEAR(CLEAR), .CLK(demux_1x8_1_out_7), .out_5(registrador_8bits_5_out_5));
  registrador_8bits registrador_8bits_6 (
    .in_1(INPUT), .PRESET(PRESET), .CLEAR(CLEAR), .CLK(demux_1x8_1_out_8), .out_5(registrador_8bits_6_out_5));
  registrador_8bits registrador_8bits_7 (
    .in_1(INPUT), .PRESET(PRESET), .CLEAR(CLEAR), .CLK(demux_1x8_1_out_9), .out_5(registrador_8bits_7_out_5));
  registrador_8bits registrador_8bits_8 (
    .in_1(INPUT), .PRESET(PRESET), .CLEAR(CLEAR), .CLK(demux_1x8_1_out_10), .out_5(registrador_8bits_8_out_5));
  multiplexador_8x1_8bits multiplexador_8x1_8bits_1 (
    .in_1(registrador_8bits_1_out_5), .in_2(registrador_8bits_2_out_5), .in_3(registrador_8bits_3_out_5),
    .in_4(registrador_8bits_4_out_5), .in_5(registrador_8bits_5_out_5), .in_6(registrador_8bits_6_out_5),
    .in_7(registrador_8bits_7_out_5), .in_8(registrador_8bits_8_out_5), .in_9(in_1), .out_10(out_5));
endmodule
