// Logisim project banco_registrador.circ as structural Verilog: 6 circuits, main circuit main
module main (
  input  [7:0] entrada,
  input  CLOCK,
  output [7:0] SAIDA
);

  and and_1 (SAIDA[0], entrada[0], CLOCK);
  and and_2 (SAIDA[1], entrada[1], CLOCK);
  and and_3 (SAIDA[2], entrada[2], CLOCK);
  and and_4 (SAIDA[3], entrada[3], CLOCK);
  and and_5 (SAIDA[4], entrada[4], CLOCK);
  and and_6 (SAIDA[5], entrada[5], CLOCK);
  and and_7 (SAIDA[6], entrada[6], CLOCK);
  and and_8 (SAIDA[7], entrada[7], CLOCK);
endmodule

module registrador (
  input  in_1,
  input  in_2,
  input  in_3,
  output [7:0] out_4,
  output [7:0] out_5
);

  jk_d jk_d_1 (.P(in_3), .D(in_3), .CLK(in_1), .C(in_2), .out_5(out_5[7]));  // open: out_6
  jk_d jk_d_2 (.P(in_3), .D(out_4[6]), .CLK(in_1), .C(in_2), .out_5(out_5[6]));  // open: out_6
  D_Flip_Flop d_ff_1 ();  // open: clk, D, Q, Qn, preset, en, reset
  jk_d jk_d_3 (.P(in_3), .D(out_4[5]), .CLK(in_1), .C(in_2), .out_5(out_5[5]));  // open: out_6
  jk_d jk_d_4 (.P(in_3), .D(out_4[4]), .CLK(in_1), .C(in_2), .out_5(out_5[4]));  // open: out_6
  jk_d jk_d_5 (.P(in_3), .D(out_4[3]), .CLK(in_1), .C(in_2), .out_5(out_5[3]), .out_6(out_5[3]));
  // jk_d jk_d_6: pin names not known; wires that end beside it: out_5[5], out_5[5], in_3, out_4[2], in_1, in_2, out_5[2]
  jk_d jk_d_7 (.P(in_3), .D(out_4[0]), .CLK(in_1), .C(in_2), .out_5(out_5[0]));  // open: out_6
  jk_d jk_d_8 (.P(in_3), .D(out_4[1]), .CLK(in_1), .C(in_2), .out_5(out_5[1]), .out_6(out_5[1]));

  assign out_4[7] = in_3;
endmodule

module jk_d (
  input  P,
  input  D,
  input  CLK,
  input  C,
  output out_5,
  output out_6
);

  wire nand_1_out, nand_2_out, nand_3_out, nand_4_out, nand_5_out, nand_6_out, not_1_out, not_2_out;

  not not_1 (not_1_out, D);
  not not_2 (not_2_out, CLK);
  nand nand_1 (nand_1_out, D, CLK, out_6);
  nand nand_2 (nand_2_out, not_1_out, out_5, CLK);
  nand nand_3 (nand_3_out, P, nand_4_out, nand_1_out);
  nand nand_4 (nand_4_out, nand_3_out, C, nand_2_out);
  nand nand_5 (nand_5_out, nand_3_out, not_2_out);
  nand nand_6 (nand_6_out, nand_4_out, not_2_out);
  nand nand_7 (out_5, P, out_6, nand_5_out);
  nand nand_8 (out_6, nand_6_out, nand_6_out, out_5, C);
endmodule

module res (
  input  [7:0] entrada,
  input  A,
  input  B,
  input  C,
  input  in_5,
  output [7:0] A1,
  output [7:0] A2,
  output [7:0] A3,
  output [7:0] A4,
  output [7:0] A5,
  output [7:0] A6,
  output [7:0] A7,
  output [7:0] A8
);

  wire demultiplex_1_out_5, demultiplex_1_out_6, demultiplex_1_out_7, demultiplex_1_out_8,
       demultiplex_1_out_10, demultiplex_1_out_11, demultiplex_1_out_12;

  demultiplex demultiplex_1 (
    .in_1(A), .in_2(B), .in_3(C), .R(in_5), .out_5(demultiplex_1_out_5), .out_6(demultiplex_1_out_6),
    .out_7(demultiplex_1_out_7), .out_8(demultiplex_1_out_8), .out_9(demultiplex_1_out_5),
    .out_10(demultiplex_1_out_10), .out_11(demultiplex_1_out_11), .out_12(demultiplex_1_out_12));
  main main_1 (.SAIDA(A1), .entrada(entrada), .CLOCK(demultiplex_1_out_5));
  main main_2 (.SAIDA(A2), .entrada(entrada), .CLOCK(demultiplex_1_out_6));
  main main_3 (.SAIDA(A4), .entrada(entrada), .CLOCK(demultiplex_1_out_8));
  main main_4 (.SAIDA(A7), .entrada(entrada), .CLOCK(demultiplex_1_out_11));
  main main_5 (.SAIDA(A8), .entrada(entrada), .CLOCK(demultiplex_1_out_12));
  main main_6 (.SAIDA(A3), .entrada(entrada), .CLOCK(demultiplex_1_out_7));
  main main_7 (.SAIDA(A5), .entrada(entrada), .CLOCK(demultiplex_1_out_5));
  main main_8 (.SAIDA(A6), .entrada(entrada), .CLOCK(demultiplex_1_out_10));
endmodule

module demultiplex (
  input  in_1,
  input  in_2,
  input  in_3,
  input  R,
  output out_5,
  output out_6,
  output out_7,
  output out_8,
  output out_9,
  output out_10,
  output out_11,
  output out_12
);

  wire and_1_out, and_2_out, and_3_out, and_4_out, and_5_out, and_6_out, and_7_out, and_8_out, not_1_out,
       not_2_out, not_3_out, not_4_out, not_5_out, not_6_out, not_7_out, not_8_out, not_9_out, not_10_out,
       not_11_out, not_12_out;

  not not_1 (not_1_out, in_1);
  not not_2 (not_2_out, in_2);
  not not_3 (not_3_out, in_3);
  not not_4 (not_4_out, in_1);
  not not_5 (not_5_out, in_2);
  not not_6 (not_6_out, in_1);
  not not_7 (not_7_out, in_3);
  not not_8 (not_8_out, in_1);
  not not_9 (not_9_out, in_2);
  not not_10 (not_10_out, in_3);
  not not_11 (not_11_out, in_2);
  not not_12 (not_12_out, in_3);
  and and_1 (and_1_out, not_1_out, not_2_out, not_3_out);
  and and_2 (and_2_out, not_4_out, not_5_out, in_3);
  and and_3 (and_3_out, not_6_out, in_2, not_7_out);
  and and_4 (and_4_out, not_8_out, in_2, in_3);
  and and_5 (and_5_out, in_1, not_9_out, not_10_out);
  and and_6 (and_6_out, in_1, not_11_out, in_3);
  and and_7 (and_7_out, in_1, in_2, not_12_out);
  and and_8 (and_8_out, in_1, in_2, in_3);
  and and_9 (out_5, R, and_1_out);
  and and_10 (out_6, R, and_2_out);
  and and_11 (out_7, R, and_3_out);
  and and_12 (out_8, R, and_4_out);
  and and_13 (out_9, R, and_5_out);
  and and_14 (out_10, R, and_6_out);
  and and_15 (out_11, R, and_7_out);
  and and_16 (out_12, R, and_8_out);
endmodule

module mult (
  input  A,
  input  B,
  input  C,
  input  in_4,
  input  in_5,
  input  in_6,
  input  in_7,
  input  in_8,
  input  in_9,
  input  in_10,
  input  in_11,
  output out_12
);

  wire and_1_out, and_2_out, and_3_out, and_4_out, and_5_out, and_6_out, and_7_out, and_8_out, and_9_out,
       and_10_out, and_11_out, and_12_out, and_13_out, and_14_out, and_15_out, and_16_out, not_1_out,
       not_2_out, not_3_out, not_4_out, not_5_out, not_6_out, not_7_out, not_8_out, not_9_out, not_10_out,
       not_11_out, not_12_out;

  not not_1 (not_1_out, A);
  not not_2 (not_2_out, B);
  not not_3 (not_3_out, C);
  not not_4 (not_4_out, A);
  not not_5 (not_5_out, B);
  not not_6 (not_6_out, A);
  not not_7 (not_7_out, C);
  not not_8 (not_8_out, A);
  not not_9 (not_9_out, B);
  not not_10 (not_10_out, C);
  not not_11 (not_11_out, B);
  not not_12 (not_12_out, C);
  and and_1 (and_1_out, not_1_out, not_2_out, not_3_out);
  and and_2 (and_2_out, not_4_out, not_5_out, C);
  and and_3 (and_3_out, not_6_out, B, not_7_out);
  and and_4 (and_4_out, not_8_out, B, C);
  and and_5 (and_5_out, A, not_9_out, not_10_out);
  and and_6 (and_6_out, A, not_11_out, C);
  and and_7 (and_7_out, A, B, not_12_out);
  and and_8 (and_8_out, C, B, A);
  and and_9 (and_9_out, in_4, and_1_out);
  and and_10 (and_10_out, in_5, and_2_out);
  and and_11 (and_11_out, and_3_out, in_6);
  and and_12 (and_12_out, and_4_out, in_7);
  and and_13 (and_13_out, and_5_out, in_8);
  and and_14 (and_14_out, and_6_out, in_9);
  and and_15 (and_15_out, and_7_out, in_10);
  and and_16 (and_16_out, and_8_out, in_11);
  or or_1 (out_12, and_9_out, and_10_out, and_11_out, and_12_out, and_13_out, and_14_out, and_15_out, and_16_out);
endmodule
