// Logisim project somador_8bits.circ as structural Verilog: 2 circuits, main circuit somador
module somador (
  input  A,
  input  B,
  input  Te,
  output S,
  output Ts
);

  wire and_1_out, and_2_out, and_3_out, xor_1_out;

  xor xor_1 (xor_1_out, A, B);
  and and_1 (and_1_out, B, Te);
  and and_2 (and_2_out, Te, A);
  and and_3 (and_3_out, B, A);
  xor xor_2 (S, xor_1_out, Te);
  or or_1 (Ts, and_1_out, and_2_out, and_3_out);
endmodule

module somador_8bits (
  input  in_1,
  input  [7:0] A0,
  input  [7:0] A1,
  output [7:0] out_4,
  output Estouro
);

  wire somador_1_ts, somador_2_ts, somador_3_ts, somador_4_ts, somador_5_ts, somador_6_ts, somador_7_ts;

  somador somador_1 (.A(A0[0]), .B(A1[0]), .Te(in_1), .S(out_4[0]), .Ts(somador_1_ts));
  somador somador_2 (.A(A0[1]), .B(A1[1]), .Te(somador_1_ts), .S(out_4[1]), .Ts(somador_2_ts));
  somador somador_3 (.A(A0[2]), .B(A1[2]), .Te(somador_2_ts), .S(out_4[2]), .Ts(somador_3_ts));
  somador somador_4 (.A(A0[3]), .B(A1[3]), .Te(somador_3_ts), .S(out_4[3]), .Ts(somador_4_ts));
  somador somador_5 (.A(A0[4]), .B(A1[4]), .Te(somador_4_ts), .S(out_4[4]), .Ts(somador_5_ts));
  somador somador_6 (.A(A0[5]), .B(A1[5]), .Te(somador_5_ts), .S(out_4[5]), .Ts(somador_6_ts));
  somador somador_7 (.A(A0[6]), .B(A1[6]), .Te(somador_6_ts), .S(out_4[6]), .Ts(somador_7_ts));
  somador somador_8 (.A(A0[7]), .B(A1[7]), .Te(somador_7_ts), .S(out_4[7]), .Ts(Estouro));
endmodule
