// Logisim project sequência_binária_101.circ as structural Verilog: 1 circuit, main circuit main
module main (
  input  [7:0] Entrada,
  output S
);

  wire and_1_out, and_2_out, and_3_out, and_4_out, and_5_out, and_6_out, and_7_out, not_1_out, not_2_out,
       not_3_out, not_4_out, not_5_out, not_6_out, not_7_out;

  not not_1 (not_1_out, Entrada[7]);
  and and_1 (and_1_out, Entrada[7], not_1_out, Entrada[6]);
  not not_2 (not_2_out, Entrada[6]);
  not not_3 (not_3_out, Entrada[5]);
  and and_2 (and_2_out, Entrada[7], not_2_out, Entrada[5]);
  and and_3 (and_3_out, Entrada[6], not_3_out, Entrada[4]);
  not not_4 (not_4_out, Entrada[4]);
  and and_4 (and_4_out, Entrada[5], not_4_out, Entrada[3]);
  not not_5 (not_5_out, Entrada[3]);
  not not_6 (not_6_out, Entrada[2]);
  and and_5 (and_5_out, not_5_out, Entrada[2]);
  and and_6 (and_6_out, Entrada[3], not_6_out, Entrada[1]);
  not not_7 (not_7_out, Entrada[1]);
  and and_7 (and_7_out, Entrada[2], not_7_out, Entrada[0]);
  or or_1 (S, and_7_out, and_6_out, and_5_out, and_4_out, and_3_out, and_2_out, and_1_out);
endmodule
